# Fritzing sketch PWM-NodeMCU (saved by Fritzing 0.9.5d)
breadboards: 1

parts:
  U1 = ESP8266 NodeMCU LoLin module
  R1 = Resistor [tolerance=±5% resistance=330 package="2010 [SMD]"]
  LED1 = LED - 5mm [color="Red (633nm)" package="5 mm [THT]"]

nets:
  N1: U1.GND, R1.Pin_0
  N2: U1.D6, LED1.anode
  N3: R1.Pin_1, LED1.cathode

custom parts:
  ESP8266 NodeMCU LoLin module: ESP8266 based NodeMCU
