# Fritzing sketch led-interrupts (saved by Fritzing 0.9.5d)
breadboards: 1

parts:
  U1 = ESP8266 NodeMCU LoLin module
  LED1 = LED - 5mm [color="Red (633nm)" package="5 mm [THT]"]
  R1 = Resistor [tolerance=±5% resistance=220 package="2010 [SMD]"]
  S1 = Pushbutton [package="[THT]"]

nets:
  N1: U1.GND, R1.Pin_0, S1.Pin_3, S1.Pin_4
  N2: U1.D5, S1.Pin_1, S1.Pin_2
  N3: U1.D6, LED1.anode
  N4: LED1.cathode, R1.Pin_1

custom parts:
  ESP8266 NodeMCU LoLin module: ESP8266 based NodeMCU
